// Logisim project 2.circ as structural Verilog: 2 circuits, main circuit main
module main (
  input  [7:0] in_1,
  input  [3:0] in_2,
  input  in_3,
  input  in_4,
  input  in_5,
  output [7:0] out_6
);

  wire clock_1_out, not_1_out;

  Clock clock_1 (.out(clock_1_out));
  RAM #(.addrWidth(4)) ram_1 (.addr(in_2), .data(out_6), .sel(in_3), .clk(clock_1_out), .ld(in_4), .clr(in_5));
  assign out_6 = not_1_out ? in_1 : 8'bz;  // Controlled_Buffer controlled_buffer_1
  not not_1 (not_1_out, in_4);
  DotMatrix #(.matrixcols(8), .matrixrows(1)) dotmatrix_1 (
    .col0(out_6[0]), .col1(out_6[1]), .col2(out_6[2]), .col3(out_6[3]), .col4(out_6[4]), .col5(out_6[5]),
    .col6(out_6[6]), .col7(out_6[7]));
endmodule

module _3 (
  input  in_1,
  input  in_2,
  input  in_3,
  input  in_4,
  input  in_5,
  input  in_6,
  input  in_7,
  input  in_8,
  input  in_9,
  output [7:0] out_10,
  output [7:0] out_11
);

  wire clock_1_out, clock_2_out, clock_3_out, clock_4_out, clock_5_out, j_k_ff_1_qn, j_k_ff_2_qn,
       j_k_ff_3_qn, not_1_out, not_2_out, not_3_out;
  wire [3:0] counter_1_q, j_k_ff_1_q;
  wire [7:0] counter_2_q, rom_1_data, rom_2_data;

  Clock clock_1 (.out(clock_1_out));
  not not_1 (not_1_out, in_9);
  J_K_Flip_Flop j_k_ff_1 (
    .J(in_9), .clk(clock_1_out), .K(not_1_out), .Q(j_k_ff_1_q[0]), .Qn(j_k_ff_1_qn));  // open: preset, en, reset
  Clock clock_2 (.out(clock_2_out));
  J_K_Flip_Flop j_k_ff_2 (
    .J(j_k_ff_1_qn), .clk(clock_1_out), .K(j_k_ff_1_qn), .Q(j_k_ff_1_q[1]), .Qn(j_k_ff_2_qn));  // open: preset, en, reset
  RAM #(.addrWidth(4)) ram_1 (.addr(j_k_ff_1_q), .data(out_11), .sel(in_6), .clk(clock_2_out), .ld(in_7), .clr(in_8));
  J_K_Flip_Flop j_k_ff_3 (
    .J(j_k_ff_2_qn), .clk(clock_1_out), .K(j_k_ff_2_qn), .Q(j_k_ff_1_q[2]), .Qn(j_k_ff_3_qn));  // open: preset, en, reset
  ROM #(.addrWidth(4)) rom_1 (.addr(j_k_ff_1_q), .data(rom_1_data), .sel(in_3));
  assign out_11 = not_2_out ? rom_1_data : 8'bz;  // Controlled_Buffer controlled_buffer_1
  not not_2 (not_2_out, in_7);
  J_K_Flip_Flop j_k_ff_4 (
    .J(j_k_ff_3_qn), .clk(clock_1_out), .K(j_k_ff_3_qn), .Q(j_k_ff_1_q[3]));  // open: Qn, preset, en, reset
  DotMatrix #(.matrixcols(8), .matrixrows(1)) dotmatrix_1 (
    .col0(out_11[0]), .col1(out_11[1]), .col2(out_11[2]), .col3(out_11[3]), .col4(out_11[4]),
    .col5(out_11[5]), .col6(out_11[6]), .col7(out_11[7]));
  Clock clock_3 (.out(clock_3_out));
  Counter #(.width(4), .max('h9)) counter_1 (.Q(counter_1_q), .clk(clock_3_out));  // open: load, D, count, carry, clr
  Counter #(.max('h9)) counter_2 (.Q(counter_2_q), .clk(clock_4_out));  // open: load, D, count, carry, clr
  Clock clock_4 (.out(clock_4_out));
  Clock clock_5 (.out(clock_5_out));
  RAM #(.addrWidth(4)) ram_2 (.addr(counter_1_q), .data(out_10), .sel(in_2), .clk(clock_5_out), .ld(in_4), .clr(in_5));
  ROM rom_2 (.addr(counter_2_q), .data(rom_2_data), .sel(in_1));
  assign out_10 = not_3_out ? rom_2_data : 8'bz;  // Controlled_Buffer controlled_buffer_2
  not not_3 (not_3_out, in_4);
  DotMatrix #(.matrixcols(8), .matrixrows(1)) dotmatrix_2 (
    .col0(out_10[0]), .col1(out_10[1]), .col2(out_10[2]), .col3(out_10[3]), .col4(out_10[4]),
    .col5(out_10[5]), .col6(out_10[6]), .col7(out_10[7]));

  // Notes on the sheet:
  //   RAM
  //   ROM
  //   contents of rom_1 (hex, n*v repeats v):
  //   2 4 6 8 10 12 14 16 18 20
  //   RAM
  //   ROM
  //   contents of rom_2 (hex, n*v repeats v):
  //   2 4 6 8 10 12 14 16 18 20
endmodule
