// Logisim project srflipflop.circ as structural Verilog: 1 circuit, main circuit main
module main (
  input  in_1,
  output out_2,
  output out_3,
  output out_4
);

  wire clock_1_out, not_1_out, s_r_ff_1_qn, s_r_ff_2_qn, s_r_ff_3_qn;

  Clock clock_1 (.out(clock_1_out));
  not not_1 (not_1_out, in_1);
  S_R_Flip_Flop s_r_ff_1 (
    .S(in_1), .clk(clock_1_out), .R(not_1_out), .Q(out_2), .Qn(s_r_ff_1_qn));  // open: preset, reset, en
  S_R_Flip_Flop s_r_ff_2 (
    .S(out_2), .clk(clock_1_out), .R(s_r_ff_1_qn), .Q(out_3), .Qn(s_r_ff_2_qn));  // open: preset, reset, en
  S_R_Flip_Flop s_r_ff_3 (
    .S(out_3), .clk(clock_1_out), .R(s_r_ff_2_qn), .Q(out_4), .Qn(s_r_ff_3_qn));  // open: preset, reset, en
endmodule
