// Logisim project 2.circ as structural Verilog: 3 circuits, main circuit main
module main (
  input  A,
  input  B,
  output sum,
  output Co
);

  wire and_1_out, and_2_out, not_1_out, not_2_out;

  not not_1 (not_1_out, A);
  not not_2 (not_2_out, B);
  and and_1 (and_1_out, not_1_out, B);
  and and_2 (and_2_out, A, not_2_out);
  and and_3 (Co, A, B);
  or or_1 (sum, and_1_out, and_2_out);
endmodule

module _3 (
  input  A,
  input  B,
  input  A_2,
  input  B_2,
  output out_5,
  output out_6,
  output _1,
  output _2__3,
  output _2,
  output _3
);

  wire not_1_out, not_2_out, not_3_out, not_4_out, or_1_out, or_2_out;

  not not_1 (not_1_out, A_2);
  not not_2 (not_2_out, B_2);
  and and_1 (out_5, not_1_out, not_2_out);
  and and_2 (_1, not_1_out, B_2);
  and and_3 (_2, A_2, not_2_out);
  and and_4 (_3, A_2, B_2);
  not not_3 (not_3_out, A);
  not not_4 (not_4_out, B);
  or or_1 (or_1_out, B, not_4_out);
  or or_2 (or_2_out, B, not_4_out);
  and and_5 (out_6, not_3_out, or_1_out);
  and and_6 (_2__3, A, or_2_out);

  // Notes on the sheet:
  //   0
  //   0, 1
endmodule

module _4 (
  input  A,
  input  B,
  input  C,
  input  D
);

  wire and_1_out, and_2_out, and_3_out, and_4_out, not_1_out, not_2_out, not_3_out, not_4_out, or_1_out,
       or_2_out;

  not not_1 (not_1_out, A);
  not not_2 (not_2_out, B);
  not not_3 (not_3_out, C);
  not not_4 (not_4_out, D);
  and and_1 (and_1_out, not_4_out, not_2_out);
  and and_2 (and_2_out, not_3_out, not_2_out, A);
  and and_3 (and_3_out, D, B);
  or or_1 (or_1_out, and_3_out, C, and_1_out);
  or or_2 (or_2_out, and_2_out, and_4_out);
  and and_4 (and_4_out, or_1_out, not_1_out);
  _7_Segment_Display u_7_segment_display_1 (.a(or_2_out));  // open: g, f, b, e, d, c, dp

  // Notes on the sheet:
  //   A
  //   B
  //   C
  //   D
  //   nA
  //   nB
  //   nC
  //   nD
endmodule
