// Logisim project 12.circ as structural Verilog: 2 circuits, main circuit main
module main (
  input  in_1,
  input  in_2,
  output out_3,
  output out_4,
  output out_5
);

  wire clock_1_out, j_k_ff_2_qn, j_k_ff_3_qn;

  Clock clock_1 (.out(clock_1_out));
  J_K_Flip_Flop j_k_ff_1 (
    .J(j_k_ff_2_qn), .clk(j_k_ff_2_qn), .K(j_k_ff_2_qn), .Q(out_3));  // open: Qn, preset, en, reset
  J_K_Flip_Flop j_k_ff_2 (
    .J(j_k_ff_3_qn), .clk(j_k_ff_3_qn), .K(j_k_ff_3_qn), .Q(out_4), .Qn(j_k_ff_2_qn));  // open: preset, en, reset
  J_K_Flip_Flop j_k_ff_3 (
    .J(in_1), .clk(clock_1_out), .K(in_2), .Q(out_5), .Qn(j_k_ff_3_qn));  // open: preset, en, reset
endmodule

module _3 (
  input  in_1,
  input  in_2,
  input  in_3,
  input  in_4,
  input  in_5,
  input  in_6,
  input  in_7,
  input  in_8,
  input  in_9,
  input  in_10,
  input  in_11,
  input  in_12,
  output out_13,
  output out_14
);

  wire clock_1_out, clock_2_out, nand_1_out, nand_2_out, nand_3_out, nor_1_out, nor_2_out, nor_3_out,
       s_r_ff_1_q, s_r_ff_1_qn, s_r_ff_2_q, s_r_ff_2_qn, s_r_ff_3_q, s_r_ff_3_qn, s_r_ff_4_q, s_r_ff_4_qn,
       s_r_ff_5_q, s_r_ff_5_qn, s_r_ff_6_q, s_r_ff_6_qn;

  Clock clock_1 (.out(clock_1_out));
  Clock clock_2 (.out(clock_2_out));
  S_R_Flip_Flop s_r_ff_1 (
    .S(in_1), .clk(clock_1_out), .R(in_2), .Q(s_r_ff_1_q), .Qn(s_r_ff_1_qn));  // open: preset, reset, en
  S_R_Flip_Flop s_r_ff_2 (
    .S(in_3), .clk(clock_1_out), .R(in_4), .Q(s_r_ff_2_q), .Qn(s_r_ff_2_qn));  // open: preset, reset, en
  S_R_Flip_Flop s_r_ff_3 (
    .S(in_5), .clk(clock_1_out), .R(in_6), .Q(s_r_ff_3_q), .Qn(s_r_ff_3_qn));  // open: preset, reset, en
  S_R_Flip_Flop s_r_ff_4 (
    .S(in_7), .clk(clock_2_out), .R(in_8), .Q(s_r_ff_4_q), .Qn(s_r_ff_4_qn));  // open: preset, reset, en
  S_R_Flip_Flop s_r_ff_5 (
    .S(in_9), .clk(clock_2_out), .R(in_10), .Q(s_r_ff_5_q), .Qn(s_r_ff_5_qn));  // open: preset, reset, en
  S_R_Flip_Flop s_r_ff_6 (
    .S(in_11), .clk(clock_2_out), .R(in_12), .Q(s_r_ff_6_q), .Qn(s_r_ff_6_qn));  // open: preset, reset, en
  nor nor_1 (nor_1_out, s_r_ff_1_q, s_r_ff_2_qn);
  nor nor_2 (nor_2_out, s_r_ff_2_q, s_r_ff_3_qn);
  nor nor_3 (nor_3_out, s_r_ff_1_qn, s_r_ff_3_q);
  nand nand_1 (nand_1_out, s_r_ff_4_q, s_r_ff_4_q, s_r_ff_5_qn);
  nand nand_2 (nand_2_out, s_r_ff_5_q, s_r_ff_6_qn);
  nand nand_3 (nand_3_out, s_r_ff_4_qn, s_r_ff_6_q);
  nor nor_4 (out_13, nor_1_out, nor_2_out, nor_3_out);
  nand nand_4 (out_14, nand_1_out, nand_1_out, nand_2_out, nand_2_out, nand_3_out);

  // Notes on the sheet:
  //   all three must have same 01 or 10 inputs
  //   two must have same 10 or 01 inputs and one must have the opposite
endmodule
